// Logisim project SequentialDivider.circ as structural Verilog: 1 circuit, main circuit Divider
module Divider (
  input  RESET,
  input  [3:0] Dividend,
  input  [3:0] Divisor,
  output [3:0] Quotient,
  output [3:0] Remainder,
  output DONE,
  output [7:0] out_7,
  output [7:0] out_8,
  output [7:0] out_9
);

  wire clock_1_out, nor_1_out, not_1_out, not_2_out, subtractor_1_bout;
  wire [2:0] adder_1_out, Counter_q;
  wire [7:0] multiplexer_1_out, multiplexer_2_out;

  Clock clock_1 (.out(clock_1_out));
  not not_1 (not_1_out, nor_1_out);
  // Shift_Register Divisor_Register: pin names not known; wires that end beside it: Dividend[3], RESET, not_1_out, clock_1_out, 1'b0, 1'b0, 1'b0, 1'b0, 1'b0
  Multiplexer #(.enable("false"), .width(8)) multiplexer_1 (
    .in0(multiplexer_2_out), .in1({4'b0000, Dividend}), .out(multiplexer_1_out), .sel(nor_1_out));
  Register Dividend_Remainder (.D(multiplexer_1_out), .clk(clock_1_out), .Q(out_7), .clr(RESET));  // open: en
  not not_2 (not_2_out, subtractor_1_bout);
  nor nor_1 (nor_1_out, out_7[0], out_7[1], out_7[2], out_7[3], out_7[4], out_7[5], out_7[6], out_7[7]);
  Multiplexer #(.enable("false"), .width(8)) multiplexer_2 (
    .in0(out_8), .in1(out_7), .out(multiplexer_2_out), .sel(subtractor_1_bout));
  Subtractor subtractor_1 (.a(out_7), .b(out_9), .out(out_8), .bout(subtractor_1_bout));  // open: bin
  // Shift_Register #(.length(4)) Quotient_Register: pin names not known; wires that end beside it: RESET, clock_1_out, clock_1_out, not_2_out, 1'b0, 1'b0, 1'b0, 1'b0, Quotient[0], Quotient[1], Quotient[2], Quotient[3]
  Register #(.width(3)) Counter (.D(adder_1_out), .en(clock_1_out), .Q(Counter_q), .clr(RESET));  // open: clk
  Adder #(.width(3)) adder_1 (.a(Counter_q), .b(3'b001), .out(adder_1_out));  // open: cin, cout
  and and_1 (DONE, adder_1_out[0], adder_1_out[1], adder_1_out[2]);

  assign Remainder = out_7[3:0];

  // Notes on the sheet:
  //   Lucas Chew, 260971542
endmodule
