// Logisim project SequentialMultipler.circ as structural Verilog: 1 circuit, main circuit Multiplier
module Multiplier (
  input  RESET,
  input  [3:0] A,
  input  [3:0] B,
  input  in_4,
  input  in_5,
  output [7:0] PRODUCT,
  output DONE
);

  wire clock_1_out, Multiplicand_p9, Multiplicand_p10, Multiplicand_p11, Multiplicand_p12;
  wire [7:0] multiplexer_1_out, Result_q, undriven;

  Clock clock_1 (.out(clock_1_out));
  // Shift_Register Multiplier: pin names not known; wires that end beside it: RESET, clock_1_out, clock_1_out, in_4, in_4, in_4, in_4, in_4
  // Shift_Register Multiplicand: pin names not known; wires that end beside it: RESET, clock_1_out, clock_1_out, in_5, in_5, in_5, in_5, in_5, Multiplicand_p9, Multiplicand_p10, Multiplicand_p11, Multiplicand_p12
  Register Result (.D(PRODUCT), .Q(Result_q), .clk(clock_1_out), .clr(RESET));  // open: en
  nor nor_1 (DONE, Multiplicand_p9, Multiplicand_p10, Multiplicand_p11, Multiplicand_p12);
  Multiplexer #(.enable("false"), .width(8)) multiplexer_1 (
    .in0({8{1'b0}}), .in1(undriven), .out(multiplexer_1_out), .sel(Multiplicand_p12));
  Adder adder_1 (.a(multiplexer_1_out), .b(Result_q), .out(PRODUCT));  // open: cin, cout

  // Notes on the sheet:
  //   Lucas Chew, 260971542
  //   Most -> Least Sig
  //   Least -> Most Sig
endmodule
