// Logisim project led.circ as structural Verilog: 1 circuit, main circuit main
module main (
);

  wire and_1_out, and_2_out, and_3_out, and_4_out, and_5_out, and_6_out, and_7_out, and_8_out, and_9_out,
       and_10_out, and_11_out, and_12_out, and_13_out, and_14_out, and_15_out, and_16_out, and_17_out,
       clock_1_out, d_ff_1_q, d_ff_1_qn, d_ff_2_q, d_ff_2_qn, d_ff_3_q, d_ff_3_qn, d_ff_4_q, d_ff_4_qn,
       not_1_out, not_2_out, not_3_out, not_4_out, not_5_out, not_6_out, not_7_out, not_8_out, not_9_out,
       undriven, undriven_2;

  Clock clock_1 (.out(clock_1_out));
  D_Flip_Flop d_ff_1 (.clk(clock_1_out), .D(d_ff_1_qn), .Q(d_ff_1_q), .Qn(d_ff_1_qn));  // open: preset, reset
  not not_1 (not_1_out, d_ff_1_q);
  D_Flip_Flop d_ff_2 (.clk(d_ff_1_qn), .D(d_ff_2_qn), .Q(d_ff_2_q), .Qn(d_ff_2_qn));  // open: preset, reset
  not not_2 (not_2_out, d_ff_2_q);
  and and_1 (and_1_out, d_ff_2_q, d_ff_1_q);
  not not_3 (not_3_out, d_ff_3_q);
  and and_2 (and_2_out, d_ff_1_q, not_2_out);
  not not_4 (not_4_out, d_ff_3_q);
  D_Flip_Flop d_ff_3 (.clk(d_ff_2_qn), .D(d_ff_3_qn), .Q(d_ff_3_q), .Qn(d_ff_3_qn));  // open: preset, reset
  and and_3 (and_3_out, not_3_out, and_2_out);
  and and_4 (and_4_out, d_ff_2_q, not_1_out);
  D_Flip_Flop d_ff_4 (.clk(d_ff_3_qn), .D(d_ff_4_qn), .Q(d_ff_4_q), .Qn(d_ff_4_qn));  // open: preset, reset
  and and_5 (and_5_out, d_ff_3_q, d_ff_2_q);
  and and_6 (and_6_out, not_4_out, and_1_out);
  and and_7 (and_7_out, not_4_out, and_4_out);
  and and_8 (and_8_out, d_ff_2_q, d_ff_1_q);
  not not_5 (not_5_out, d_ff_2_q);
  not not_6 (not_6_out, d_ff_1_q);
  and and_9 (and_9_out, not_6_out, d_ff_4_q);
  and and_10 (and_10_out, and_5_out, not_1_out);
  and and_11 (and_11_out, d_ff_3_q, and_8_out);
  not not_7 (not_7_out, d_ff_3_q);
  and and_12 (and_12_out, not_5_out, and_9_out);
  LED led_1 (.in(and_6_out));
  and and_13 (and_13_out, not_7_out, and_12_out);
  LED led_2 (.in(and_10_out));
  LED led_3 (.in(and_3_out));
  not not_8 (not_8_out, d_ff_1_q);
  not not_9 (not_9_out, d_ff_2_q);
  LED led_4 (.in(and_13_out));
  LED led_5 (.in(undriven));
  and and_14 (and_14_out, not_8_out, not_9_out);
  LED led_6 (.in(and_11_out));
  LED led_7 (.in(and_7_out));
  and and_15 (and_15_out, d_ff_1_q, not_9_out);
  and and_16 (and_16_out, and_14_out, d_ff_3_q);
  LED led_8 (.in(and_17_out));
  LED led_9 (.in(undriven_2));
  and and_17 (and_17_out, and_15_out, d_ff_3_q);
  LED led_10 (.in(and_16_out));

  // Notes on the sheet:
  //   Only the first 9 numbers work. Past that is random
  //   1
  //   0
  //   2
  //   3
  //   Lucas Chew, 260971542
  //   5
  //   4
  //   6
  //   7
  //   8
  //   9
endmodule
